# Fritzing sketch alarm_scheme (saved by Fritzing 0.9.3b)
breadboards: 1

parts:
  LED2 = LED - 5mm [color="Red (633nm)" package="5 mm [THT]"]
  LED3 = LED - 5mm [color="Red (633nm)" package="5 mm [THT]"]
  LED4 = LED - 5mm [color="Red (633nm)" package="5 mm [THT]"]
  LED5 = LED - 5mm [color="Red (633nm)" package="5 mm [THT]"]
  LED6 = LED - 5mm [color="Red (633nm)" package="5 mm [THT]"]
  LED7 = LED - 5mm [color="Red (633nm)" package="5 mm [THT]"]
  LED8 = LED - 5mm [color="Red (633nm)" package="5 mm [THT]"]
  LED9 = LED - 5mm [color="Red (633nm)" package="5 mm [THT]"]
  LED10 = LED - 5mm [color="Red (633nm)" package="5 mm [THT]"]
  LED11 = LED - 5mm [color="Red (633nm)" package="5 mm [THT]"]
  R1 = Resistor [tolerance=±5% resistance=220 package=THT]
  R2 = Resistor [tolerance=±5% resistance=220 package=THT]
  R3 = Resistor [tolerance=±5% resistance=220 package=THT]
  R4 = Resistor [tolerance=±5% resistance=220 package=THT]
  R5 = Resistor [tolerance=±5% resistance=220 package=THT]
  Часть1 = Arduino Uno (Rev3)
  IC1 = DS1302 [package="SO8 [SMD]"]
  R6 = Resistor [tolerance=±5% resistance=220 package=THT]
  J1 = Piezo Speaker
  R7 = Photocell (LDR) [package=THT]
  R8 = Resistor [tolerance=±5% resistance=220 package=THT]
  Часть2 = Bluetooth HC-05 Macho

nets:
  N1: LED2.cathode, LED3.anode
  N2: LED2.anode, Часть1.D13/SCK
  N3: LED3.cathode, R1.Pin_1
  N4: LED4.cathode, LED5.anode
  N5: LED4.anode, Часть1.D12/MISO
  N6: LED5.cathode, R2.Pin_1
  N7: LED6.cathode, LED7.anode
  N8: LED6.anode, Часть1.D11_PWM/MOSI
  N9: LED7.cathode, R3.Pin_1
  N10: LED8.cathode, LED9.anode
  N11: LED8.anode, Часть1.D10_PWM/SS
  N12: LED9.cathode, R4.Pin_1
  N13: LED10.cathode, LED11.anode
  N14: LED10.anode, Часть1.D9_PWM
  N15: LED11.cathode, R5.Pin_1
  GND: R1.Pin_0, R2.Pin_0, R3.Pin_0, R4.Pin_0, R5.Pin_0, Часть1.GND, R6.Pin_0, J1.pin1, R8.Pin_0, Часть2.GND
  N16: Часть1.A0, R7.pin_1, R8.Pin_1
  N17: Часть1.D8, IC1.CE_-_Chip_Enable
  N18: Часть1.D0/RX, Часть2.TXD
  N19: Часть1.D1/TX, Часть2.RXD
  N20: Часть1.D3_PWM, J1.pin2
  N21: Часть1.D6_PWM, IC1.SCLK_-_SPI_Clock
  N22: Часть1.D7, IC1.I/O_-_SPI_Data_In/Out
  5V: Часть1.5V, IC1.Vbat_-_Backup_Supply, R7.pin_0, Часть2.VCC
  N23: IC1.0V, R6.Pin_1
